# Fritzing sketch Diag (saved by Fritzing 0.9.9b)

parts:
  microSD1 = MicroSD Card Module
  Part1 = Adafruit OLED Monochrome 0.91in I2C with STEMMA QT [part_number="Adafruit #4440"]
  MH-ET_Live_Minikit_for_ESP1 = MH-ET Live Minikit for ESP32
  U1 = SUP500F [package=sup500f]

nets:
  GND: microSD1.GND, Part1.GND, MH-ET_Live_Minikit_for_ESP1.GND, U1.GND
  VCC: microSD1.VCC, Part1.VCC, MH-ET_Live_Minikit_for_ESP1.3.3V, U1.VCC
  N1: microSD1.MISO, MH-ET_Live_Minikit_for_ESP1.IO19
  N2: microSD1.MOSI, MH-ET_Live_Minikit_for_ESP1.IO23
  N3: microSD1.SCK, MH-ET_Live_Minikit_for_ESP1.IO18
  N4: microSD1.CS, MH-ET_Live_Minikit_for_ESP1.IO5
  N5: Part1.SDA, MH-ET_Live_Minikit_for_ESP1.IO22
  N6: Part1.SCL, MH-ET_Live_Minikit_for_ESP1.IO21
  N7: MH-ET_Live_Minikit_for_ESP1.IO17, U1.RX-I
  N8: MH-ET_Live_Minikit_for_ESP1.IO16, U1.TX-O

custom parts:
  Adafruit OLED Monochrome 0.91in I2C with STEMMA QT: These displays are small, only about 1" diagonal, but very readable due to the high contrast of an OLED display. This display is made of 128x32 individual white OLED pixels, each one is turned on or off by the controller chip. Because the display makes its own light, no backlight is required. This reduces the power required to run the OLED and is why the display has such high contrast; we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
  MH-ET Live Minikit for ESP32: MH-ET Live Minikit for ESP32 ( http://mh.nodebb.com/topic/8/mh-et-live-minikit-for-esp32/2/) PCB footprint is invalid.
